# Fritzing sketch TiltandEcho (saved by Fritzing 0.9.3b)
breadboards: 1

parts:
  S1 = Tilt Switch [package=THT]
  Part1 = Arduino Uno (Rev3)
  hc-sr1 = hc-sr04

nets:
  GND: S1.Pin_1, S1.Pin_2, Part1.D3_PWM, Part1.GND, hc-sr1.GND
  N1: Part1.D6_PWM, hc-sr1.Trig
  N2: Part1.D7, hc-sr1.Echo
  5V: Part1.5V, hc-sr1.VCC
